# Fritzing sketch Untitled Sketch (saved by Fritzing 1.0.5)
breadboards: 1

parts:
  Part1 = Arduino Uno (Rev3)
  HC-SR04_Sensor_1 = HC-SR04 Ultrasonic Distance Sensor
  R3 = Photocell (LDR) [power=0.25W dark_resistance_@0.01lx=300kΩ light_resistance_@100lx=400Ω luminance=10lx package=THT]
  R4 = Resistor [tolerance=±5% resistance=220 package="2010 [SMD]"]
  LED_red = LED - 5mm [color="Red (633nm)" current=0.030A package="5 mm [THT]"]
  LED_green = LED - 5mm [color="Green (555nm)" current=30mA package="5 mm [THT]"]
  R5 = Resistor [tolerance=±5% power=0.25W resistance=220 package=THT]
  R6 = Resistor [tolerance=±5% power=0.25W resistance=220 package=THT]
  J1 = Piezo Speaker

nets:
  N1: Part1.A0, R3.pin_1, R4.Pin_0
  N2: Part1.D9_PWM, J1.pin2
  N3: Part1.D10_PWM/SS, R6.Pin_1
  N4: Part1.D11_PWM/MOSI, R5.Pin_1
  N5: Part1.D4, HC-SR04_Sensor_1.ECHO
  N6: Part1.D7, HC-SR04_Sensor_1.TRIG
  5V: Part1.5V, HC-SR04_Sensor_1.VCC, R3.pin_0
  GND: Part1.GND, HC-SR04_Sensor_1.GND, R4.Pin_1, LED_red.cathode, LED_green.cathode, J1.pin1
  N7: LED_red.anode, R6.Pin_0
  N8: LED_green.anode, R5.Pin_0

// code stored in the sketch: Untitled.ino
void setup() {
  // put your setup code here, to run once:
pinMode(10,OUTPUT); 
pinMode(11,OUTPUT);

}


void loop() {
  // put your main code here, to run repeatedly:

digitalWrite(11,HIGH); 
delay(500); 
digitalWrite(10,HIGH);
}
